# Fritzing sketch HealthPi (saved by Fritzing 0.9.6b)
breadboards: 1

parts:
  Raspberry_Pi_1 = Raspberry Pi 3 [part_number=RPI-3-V1.2]
  ADC1 = MCP3008 [package=dil16]
  DS1 = DS18B20 1-Wire Temperature Sensor [part_number=DS18B20]
  R1 = Resistor [tolerance=±5% resistance=4.7k package=THT]
  SEN1 = Pulse Sensor [package=SIP]
  M1 = MAX30102
  R4 = Resistor [tolerance=±5% resistance=4.7k package=THT]
  Grove_GSR = Grove Temperature Sensor

nets:
  3V3: Raspberry_Pi_1.3v3, Raspberry_Pi_1.3V3, DS1.VDD, R1.Pin_0, M1.VIN, R4.Pin_0
  N1: Raspberry_Pi_1.GPIO2, M1.SDA
  N2: Raspberry_Pi_1.GPIO3, M1.SCL
  N3: Raspberry_Pi_1.GPIO4, M1.INT, R4.Pin_1
  N4: Raspberry_Pi_1.GPIO17, DS1.DQ, R1.Pin_1
  N5: Raspberry_Pi_1.GPIO9, ADC1.Din
  N6: Raspberry_Pi_1.GPIO11, ADC1.Dout
  GND: Raspberry_Pi_1.GND, ADC1.DGND, ADC1.CLK, ADC1.AGND, DS1.GND, SEN1.GND, M1.GND, Grove_GSR.GND
  N7: Raspberry_Pi_1.GPIO8, ADC1.CS/SHDN
  VCC: Raspberry_Pi_1.5V, ADC1.VREF, ADC1.VDD, SEN1.Vcc, Grove_GSR.VCC
  N8: ADC1.CH0, SEN1.Signal
  N9: ADC1.CH3, Grove_GSR.SIG

notes:
  5 V
  3.3 V

custom parts:
  Pulse Sensor: Pulse Sensor Optical Heart Rate Monitor for Arduino and other microcontrollers
  MAX30102: Oximeter module using the MAX30102 chip. You may wish to read (and check your module) this post on power problems with these modules: https://reedpaper.wordpress.com/2018/08/22/pulse-oximeter-max30100-max30102-how-to-fix-wrong-board/ . As usual, if you want the mounting holes in pcb, you need to drag a hole over the pad in silkscreen to actually drill the hole (by default they are not drilled)
